# Fritzing sketch exp11-schematics (saved by Fritzing 0.9.3b)
perfboards: 1

parts:
  R1 = Resistor [tolerance=±5% resistance=1k package=THT]
  R2 = Resistor [tolerance=±5% resistance=1k package=THT]  # not connected
  R3 = Trimmer Potentiometer [maximum_resistance=10kΩ package=THT]
  VCC1 = Battery block 9V
  R4 = Photocell (LDR) [package=THT]
  Q3 = NPN-Transistor [package="TO92 [THT]"]
  Q4 = NPN-Transistor [package="TO92 [THT]"]
  LED1 = LED - 5mm [color="Red (633nm)" package="5 mm [THT]"]

nets:
  N1: R1.Pin_0, Q4.C
  N2: R1.Pin_1, Q3.B
  N3: R3.leg1, R3.leg2, VCC1.-, Q3.E
  N4: VCC1.+, R4.pin_1, LED1.cathode
  N5: Q3.C, LED1.anode
