# Fritzing sketch rfid-lock1 (saved by Fritzing 0.9.3b)
breadboards: 1

parts:
  Part2 = Arduino Uno (Rev3)
  Part1 = RFID USB Reader

nets:
  N1: Part2.D9_PWM, Part1.VCC
  N2: Part2.D10_PWM/SS, Part1.GNDT
  N3: Part2.D11_PWM/MOSI, Part1.ANT2
  N4: Part2.D12/MISO, Part1.ANT1
  N5: Part2.D13/SCK, Part1.CP
  N6: Part2.GND, Part1.TX-O
