# Fritzing sketch exp5-strobe-melody (saved by Fritzing 0.9.3b)
breadboards: 1

parts:
  Part1 = Arduino Uno (Rev3)
  J1 = Piezo Speaker
  LED1 = LED - 5mm [color="Red (633nm)" package="5 mm [THT]"]
  LED2 = LED - 5mm [color="Red (633nm)" package="5 mm [THT]"]
  R2 = Rotary Potentiometer (Small) [maximum_resistance=100kΩ package=THT]
  R3 = Resistor [tolerance=±5% resistance=220 package=THT]
  R4 = Resistor [tolerance=±5% resistance=220 package=THT]
  LED3 = LED - 5mm [color="Red (633nm)" package="5 mm [THT]"]
  LED4 = LED - 5mm [color="Red (633nm)" package="5 mm [THT]"]
  LED5 = LED - 5mm [color="Red (633nm)" package="5 mm [THT]"]
  R5 = Resistor [tolerance=±5% resistance=220 package=THT]
  R6 = Resistor [tolerance=±5% resistance=220 package=THT]
  R7 = Resistor [tolerance=±5% resistance=220 package=THT]
  LED6 = LED - 5mm [color="Red (633nm)" package="5 mm [THT]"]
  LED7 = LED - 5mm [color="Red (633nm)" package="5 mm [THT]"]
  LED8 = LED - 5mm [color="Red (633nm)" package="5 mm [THT]"]
  R8 = Resistor [tolerance=±5% resistance=220 package=THT]
  R9 = Resistor [tolerance=±5% resistance=220 package=THT]
  R10 = Resistor [tolerance=±5% resistance=220 package=THT]

nets:
  N1: Part1.A0, R2.wiper
  N2: Part1.D8, R7.Pin_1
  N3: Part1.D9_PWM, R6.Pin_1
  N4: Part1.D10_PWM/SS, R5.Pin_1
  N5: Part1.D11_PWM/MOSI, R4.Pin_1
  N6: Part1.D12/MISO, R3.Pin_1
  N7: Part1.D13/SCK, J1.pin2
  N8: Part1.D5_PWM, R10.Pin_1
  N9: Part1.D6_PWM, R9.Pin_1
  N10: Part1.D7, R8.Pin_1
  N11: Part1.5V, R2.leg1
  N12: Part1.GND, J1.pin1, LED1.anode, LED2.anode, R2.leg2, LED3.anode, LED4.anode, LED5.anode, LED6.anode, LED7.anode, LED8.anode
  N13: LED1.cathode, R3.Pin_0
  N14: LED2.cathode, R4.Pin_0
  N15: LED3.cathode, R5.Pin_0
  N16: LED4.cathode, R6.Pin_0
  N17: LED5.cathode, R7.Pin_0
  N18: LED6.cathode, R8.Pin_0
  N19: LED7.cathode, R9.Pin_0
  N20: LED8.cathode, R10.Pin_0
