# Fritzing sketch exp6-bagels (saved by Fritzing 0.9.3b)
breadboards: 1

parts:
  LCD1 = LCD screen
  Part1 = Arduino Uno (Rev3)
  U1 = POT [package=pot_mammoth]
  U2 = BUTTONPAD-2X2 [package=buttonpad-2x2]

nets:
  VSS: LCD1.VSS, LCD1.R/W, LCD1.LED-, Part1.GND, U1.S
  VDD: LCD1.VDD, LCD1.LED+, Part1.5V, U1.E
  N1: LCD1.V0, U1.A
  N2: LCD1.RS, Part1.D8
  N3: LCD1.E, Part1.D9_PWM
  N4: LCD1.DB4, Part1.D10_PWM/SS
  N5: LCD1.DB5, Part1.D11_PWM/MOSI
  N6: LCD1.DB6, Part1.D12/MISO
  N7: LCD1.DB7, Part1.D13/SCK
  N8: Part1.D0/RX, U2.-C1_BLU
  N9: Part1.D1/TX, U2.-C1_GRN
  N10: Part1.D2, U2.-C1_RED
  N11: Part1.D3_PWM, U2.-C1_SIG1
  N12: Part1.D4, U2.-C1_GND
  N13: Part1.D5_PWM, U2.-C2_BLU
  N14: Part1.D6_PWM, U2.-C2_RED
