# Fritzing sketch exp7-joystick-laser (saved by Fritzing 0.9.3b)
breadboards: 1

parts:
  J1 = Basic Servo
  J2 = Basic Servo
  Part1 = Arduino Leonardo (Rev3b)
  Part2 = Thumb Joystick

nets:
  GND: J1.gnd, J2.gnd, Part1.GND, Part2.GND
  VCC: J1.vcc, J2.vcc, Part1.5V, Part2.VCC
  N1: J1.pulse, Part1.D10_PWM/A10
  N2: J2.pulse, Part1.D9_PWM/A9
  N3: Part1.A0, Part2.HORZ
  N4: Part1.A1, Part2.VERT

// code stored in the sketch: joystick-controlled.ino
#include <Servo.h> // Include the Servo Library to control the servos
Servo xservo, yservo; // create servo object to control the x and y directions servo
//Servo Variables
int pos = 0;       // variable to store the servo position
int XServoPin = 10; // Servo pin that will control X motion
int YServoPin = 9; // Servo pin that will control Y motion
//Joystick variables
int xposPin = A0;    // select the input pin for the potentiometer
int yposPin = A1;    // select the input pin for the potentiometer
int Xpos = 0;
int Ypos = 0;
int buttonPin = 7;
int buttonPress = 0;
//Lazer Variables
int laserPin = 6;

void setup() {
  pinMode(laserPin,OUTPUT);      //The lazer will be an output
  pinMode(buttonPin,INPUT);      //The buttonpress pin is an input
  digitalWrite(buttonPin,HIGH);  //This enables the Arduino pullup for this pin
  
  xservo.attach(XServoPin);  // attaches the servo on pin 9 to the servo object
  yservo.attach(YServoPin);  // attaches the servo on pin 8 to the servo object
}

//buttonPress = digitalRead(buttonPin); //Read the sate of the button
//if(buttonPress == LOW) // The button press is active low , so if it is pressed we will turn the laser on
//{
  //digitalWrite(laserPin, HIGH); //Turn Laser on
//}
//else
//{
  //digitalWrite(laserPin, LOW); // If it is not pressed, keep lazer off
//}

Xpos = analogRead(xposPin);     // read and store the x position location of the joystick
Xpos = map(Xpos,0,1023,0,180);  //map the analog read x values to the 0-180 servo values
Ypos = analogRead(yposPin);     // read and store the y position of the joystick
Ypos = map(Ypos,0,1023,0,180);  //map the analog read y values to the 0-180 servo values
xservo.write(Xpos);             // move the X Location servo to the x position the joystick is at
yservo.write(Ypos);             // move the Y Location servo to the y position the joystick is at
delay(50);
