# Fritzing sketch exp8-intruder-alarm (saved by Fritzing 0.9.3b)
breadboards: 1

parts:
  Part1 = Arduino Uno (Rev3)
  hc-sr1 = hc-sr04
  J1 = Basic Servo
  R1 = Resistor [tolerance=±5% resistance=220 package="0402 [SMD]"]
  R2 = Resistor [tolerance=±5% resistance=220 package="0402 [SMD]"]
  LED2 = LED - 5mm [color="Red (633nm)" package="5 mm [THT]"]
  LED3 = LED - 5mm [color="Blue (430nm)" package="5 mm [THT]"]
  J2 = Piezo Speaker
  R3 = PHOTOCELL [package=photocell-kit]
  R4 = Resistor [tolerance=±5% resistance=220 package="2010 [SMD]"]
  U1 = MLX90614 [package=to-39]

nets:
  GND: Part1.A0, Part1.GND, hc-sr1.GND, J1.gnd, LED2.cathode, LED3.cathode, J2.pin1, R4.Pin_1, U1.PWM_SDA
  N1: Part1.D8, J2.pin2
  N2: Part1.D9_PWM, J1.pulse
  N3: Part1.D12/MISO, hc-sr1.Trig
  N4: Part1.D13/SCK, hc-sr1.Echo
  N5: Part1.D2, U1.SCL_VZ
  N6: Part1.D3_PWM, R2.Pin_1
  N7: Part1.D4, R1.Pin_1
  VCC: Part1.5V, hc-sr1.VCC, J1.vcc, R3.P$1
  N8: R1.Pin_0, LED3.anode
  N9: R2.Pin_0, LED2.anode
  N10: R3.P$2, R4.Pin_0
  VDD: U1.VDD, U1.VSS

notes:
  PIR SENSOR
  THE PIEZO BUZZER’S POSITIVE (RED) WIRE IS CONNECTED TO PIN 8 ON THE ARDUINO. THE GND (BLACK) WIRE IS CONNECTED TO GND.
  THE PHOTORESISTOR DETECTS LIGHT FROM THE LASER. WHEN THE BEAM IS BROKEN BY AN INTRUDER, THE GREEN LED TURNS OFF AND THE PIEZO BUZZER SOUNDS.
  THE SERVO ARM MOVES WHEN AN OBJECT IS DETECTED WITHIN THE SENSOR’S PERIMETER. THE SIGNAL WIRE IS CONNECTEDTO ARDUINO PIN 9.
  THE ULTRASONIC SENSOR CAN DEFINE DISTANCE. IT WILL TRIGGER AN ALARM WHEN THE PERIMETER IS BREACHED.

// code stored in the sketch: intruder-alarm.ino
#include <NewPing.h> // Call NewPing library
#include <Servo.h> // Call Servo library
#define trigPin 12 // Trig pin connected to Arduino 12
#define echoPin 13 // Echo pin connected to Arduino 13
#define MAX_DISTANCE 500
NewPing sonar(trigPin, echoPin, MAX_DISTANCE); // Library setting
int greenLed = 4, redLed = 3; // Set green LED to pin 3, red to pin 2
int pos = 20;
Servo myservo;
int buzzPin = 8; // Pin connected to the piezo
int inputPin = 2; // Pin connected to PIR sensor
int pirState = LOW; // Start PIR state LOW with no motion
int val = 0; // Variable for reading the pin status

void setup() {
	Serial.begin (115200);
	pinMode(trigPin, OUTPUT);
	pinMode(echoPin, INPUT);
	pinMode(greenLed, OUTPUT);
	pinMode(redLed, OUTPUT);
	myservo.attach(9); // Servo attached to pin 9

	pinMode(buzzPin, OUTPUT); // Set pin as output
	pinMode(inputPin, INPUT);
}
void loop() {
	int duration, distance, pos = 0, i;
	val = digitalRead(inputPin);
	digitalWrite(trigPin, LOW);
	delayMicroseconds(2);
	digitalWrite(trigPin, HIGH); // Trig pin sends a ping
	delayMicroseconds(10);
	digitalWrite(trigPin, LOW);
	duration = pulseIn(echoPin, HIGH); // Echo receives the ping
	distance = (duration / 2) / 29.1;
	Serial.print(distance);
	Serial.println(" cm");
	// If sensor detects object within 15 cm
	if (distance <= 15) || (analogRead(0) > 850) || (val == HIGH) { // you can change the distance to be closer and change the analog value depending on the
// values of your photoresistor
		digitalWrite(greenLed, LOW); // Turn off green LED
		digitalWrite(redLed, HIGH); // Turn on red LED
		myservo.write(180); // Move servo arm 180 degrees
		playTone(300, 160);  // Turn the piezo ON
		delay(1000);
		digitalWrite(redLed, LOW); // Light the red LED
		digitalWrite(buzzPin, LOW);
		myservo.write(90);
		delay(1000);
		digitalWrite(redLed, HIGH);
		myservo.write(0);
		delay(450);
		digitalWrite(redLed, LOW);
		myservo.write(90);

		if (pirState == LOW) {
			// Print to the Serial Monitor if motion detected
			Serial.println("Motion detected!");
			pirState = HIGH;
		}
}
	// Otherwise
	else {
		digitalWrite(redLed, LOW); // Turn off red LED
		digitalWrite(greenLed, HIGH); // Turn on green LED
		myservo.write(90);
		playTone(0, 0); // Turn off the piezo
		if (pirState == HIGH) {
			Serial.println("Motion ended!");
			pirState = LOW;
		}
}
	delay(450);
}

void playTone(long duration, int freq) { // Duration in ms,
	// frequency in Hz
	duration *= 1000;
	int period = (1.0 / freq) * 1000000;
	long elapsed_time = 0;
	while (elapsed_time < duration) {
		digitalWrite(buzzPin, HIGH);
		delayMicroseconds(period / 2);
		digitalWrite(buzzPin, LOW);
		delayMicroseconds(period / 2);
		elapsed_time += (period);
}
